# Fritzing sketch NFC_RTC (saved by Fritzing 0.9.3b)
breadboards: 1

parts:
  Part1 = Arduino Uno (Rev3)
  PN532_-_NFC = Arduino Prototyping Shield
  DS3231SN = Real Time Clock Module - DS1307 RTC Breakout Board
  R1 = Resistor [tolerance=±5% resistance=220 package=THT]
  Piezo = Piezo Speaker
  LED1 = LED - 5mm [color="Red (633nm)" package="5 mm [THT]"]
  VCC1 = 4 x AAA Battery Mount
  JP2 = USB_MICROB_PLUG [package=micro-b-ra-th]

nets:
  GND: Part1.GND, PN532_-_NFC.GND, DS3231SN.GND, Piezo.pin1
  N1: Part1.A4/SDA, PN532_-_NFC.SDA, DS3231SN.SDA
  N2: Part1.A5/SCL, PN532_-_NFC.SCL, DS3231SN.SCL
  N3: Part1.D2, PN532_-_NFC.D2
  N4: Part1.D3_PWM, Piezo.pin2
  N5: Part1.D4, R1.Pin_1
  5V: Part1.5V, PN532_-_NFC.+5V, DS3231SN.5V
  N6: R1.Pin_0, LED1.anode
  N7: VCC1.-, JP2.GND
  N8: VCC1.+, JP2.VCC

notes:
  IRQ
  USB power bank
  AAA or AA Size,
  5V, <TBD> mAh
