# Fritzing sketch Nano_Schematic (saved by Fritzing 0.9.3b)
breadboards: 1

parts:
  PN532_-_NFC = Arduino Prototyping Shield
  DS3231SN = Real Time Clock Module - DS1307 RTC Breakout Board
  R1 = Resistor [tolerance=±5% resistance=220 package=THT]
  Piezo = Piezo Speaker
  LED1 = LED - 5mm [color="Red (633nm)" package="5 mm [THT]"]
  VCC1 = 4 x AAA Battery Mount
  Fox_Front_View_(Female) = DB9 Connector [package=db9]
  X1 = USB Connectors [package=usb-a-s]
  X8 = USB Connectors [package=usb-a-h]
  Part3 = Arduino Nano (Rev3.0) (ICSP)
  VND5160JTR-E1 = VND5160JTR-E [part_number=VND5160JTR-E package=PowerSSO-12]

nets:
  GND: PN532_-_NFC.GND, DS3231SN.GND, Piezo.pin1, Fox_Front_View_(Female).8, Part3.GND
  N1: PN532_-_NFC.D2, Part3.D2
  3.3V: PN532_-_NFC.3.3V, DS3231SN.5V, VND5160JTR-E1.OUTPUT1
  N2: PN532_-_NFC.SDA, DS3231SN.SDA, Part3.A4
  N3: PN532_-_NFC.SCL, DS3231SN.SCL
  N4: PN532_-_NFC.RESET, Part3.D3
  N5: R1.Pin_0, LED1.anode
  N6: R1.Pin_1, Part3.D4
  N7: Piezo.pin2, Part3.D5
  N8: VCC1.-, X1.GND
  N9: VCC1.+, X1.VBUS
  N10: Fox_Front_View_(Female).6, Part3.A0
  N11: Fox_Front_View_(Female).7, Part3.D7
  N12: Fox_Front_View_(Female).9, Part3.D6
  N13: X8.VBUS, Part3.5V
  N14: Part3.D12/MISO, VND5160JTR-E1.INPUT1

notes:
  IRQ
  USB power bank
  5V, 2200 mAh
  With USB: 90 mA (NFC:100 mA) <= UNO
  Direct: 80 mA (NFC: 90 mA)
  Tx
  Rx
  Micro USB cable
  PWM (ON = OFF = 1s)
  When Starting to Tx, Signal goes low -> Boot up NFC
  When hunt finish, this signal goes high -> Turn off NFC
  There is a 0.2xx pulse here when being to Tx and before shutdown but well after and before Fox active.
  5V from fox (not used)
  RTC and NFC work on 5V
  Connect battery directly
  This avoids the regulator and the FTDI chip needed for USB
  High Side Switch 5V (harvested SMD)
  Standby = 0.9 uA
  On = 1.5 mA
  Triggered based on PWM

custom parts:
  VND5160JTR-E: High side driver used as a switch In off mode, 0.9 uA current and in use mode 1.5 mA
